// Logisim project practs.circ as structural Verilog: 1 circuit, main circuit main
module main (
  input  in_1,
  input  in_2,
  input  in_3,
  input  in_4,
  input  in_5,
  input  in_6,
  input  in_7,
  input  in_8,
  input  in_9,
  output out_10,
  output out_11,
  output out_12,
  output out_13,
  output out_14,
  output out_15
);

  wire and_2_out, and_3_out, clock_1_out, clock_2_out, clock_3_out, j_k_ff_1_qn, j_k_ff_3_qn, j_k_ff_4_qn,
       nand_1_out, nand_2_out, nand_3_out, nand_4_out, nand_5_out, nand_6_out, not_1_out, xor_2_out;

  Clock clock_1 (.out(clock_1_out));
  Clock clock_2 (.out(clock_2_out));
  not not_1 (not_1_out, clock_1_out);
  nand nand_1 (nand_1_out, out_11, in_1, clock_1_out);
  nand nand_2 (nand_2_out, clock_1_out, in_2, out_10);
  J_K_Flip_Flop j_k_ff_1 (.J(in_4), .clk(clock_2_out), .K(in_4), .Qn(j_k_ff_1_qn));  // open: Q, preset, en, reset
  xor xor_1 (out_12, in_6, in_8);
  // NOR_Gate nor_1 is placed but not wired
  and and_1 (out_14, in_6, in_8);
  nand nand_3 (nand_3_out, nand_1_out, nand_4_out);
  nand nand_4 (nand_4_out, nand_3_out, nand_2_out);
  J_K_Flip_Flop j_k_ff_2 (.J(in_4), .clk(j_k_ff_1_qn), .K(in_4));  // open: Q, Qn, preset, en, reset
  Clock clock_3 (.out(clock_3_out));
  nand nand_5 (nand_5_out, nand_3_out, not_1_out);
  nand nand_6 (nand_6_out, not_1_out, nand_4_out);
  J_K_Flip_Flop j_k_ff_3 (.J(in_3), .clk(clock_3_out), .K(in_3), .Qn(j_k_ff_3_qn));  // open: Q, preset, en, reset
  xor xor_2 (xor_2_out, in_5, in_7);
  nand nand_7 (out_10, nand_5_out, out_11);
  nand nand_8 (out_11, out_10, nand_6_out);
  J_K_Flip_Flop j_k_ff_4 (.J(in_3), .clk(j_k_ff_3_qn), .K(in_3), .Qn(j_k_ff_4_qn));  // open: Q, preset, en, reset
  xor xor_3 (out_13, xor_2_out, in_9);
  J_K_Flip_Flop j_k_ff_5 (.J(in_3), .clk(j_k_ff_4_qn), .K(in_3));  // open: Q, Qn, preset, en, reset
  and and_2 (and_2_out, xor_2_out, in_9);
  and and_3 (and_3_out, in_7, in_5);
  or or_1 (out_15, and_2_out, and_3_out);

  // Notes on the sheet:
  //   2/3 bit async counter
  //   JK Mater Slave 
endmodule
